# Fritzing sketch Hello_Ella_Drawing (saved by Fritzing 0.9.2b)
breadboards: 1

parts:
  Part1 = Arduino Uno (Rev3)
  LCD1 = LCD screen
  R1 = Resistor [tolerance=±5% resistance=10 package=THT]
  S1 = Pushbutton [package="[THT]"]
  R3 = Resistor [tolerance=±5% resistance=220 package=THT]
  R2 = Rotary Potentiometer (Small) [maximum_resistance=50Ω package=THT]

nets:
  N1: Part1.D11_PWM/MOSI, LCD1.E
  N2: Part1.D12/MISO, LCD1.R/W
  N3: Part1.D2, LCD1.DB7
  N4: Part1.D3_PWM, LCD1.DB6
  N5: Part1.D4, LCD1.DB5
  N6: Part1.D5_PWM, LCD1.DB4
  N7: Part1.D6_PWM, S1.Pin_1, S1.Pin_2, R3.Pin_0
  5V: Part1.5V, LCD1.VDD, R1.Pin_0, S1.Pin_3, S1.Pin_4, R2.leg1
  N8: Part1.GND, R3.Pin_1
  N9: LCD1.VSS, LCD1.LED-, R2.leg2
  N10: LCD1.V0, R2.wiper
  N11: LCD1.LED+, R1.Pin_1
